// Logisim project Brajcic_SimpleProcessor.circ as structural Verilog: 5 circuits, main circuit main
module main (
  input  [7:0] Mem_Address,
  input  [3:0] Instruction,
  input  [1:0] RA,
  input  [1:0] RB,
  input  [7:0] value,
  input  Store,
  input  Store_from_RA,
  input  RegSrc,
  input  [1:0] Select_register,
  input  Load_Register
);

  wire clk, demultiplexer_1_out0, demultiplexer_1_out1, demultiplexer_1_out2, demultiplexer_1_out3,
       not_1_out, reset;
  wire [3:0] controlled_buffer_1_out, controlled_buffer_1_out_2, multiplexer_4_out, multiplexer_4_out_2;
  wire [7:0] ALUout, multiplexer_1_out, multiplexer_2_out, R0_q, R1_q, R2_q, R3_q, Rstr;

  Multiplexer #(.width(8)) multiplexer_1 (
    .in0({controlled_buffer_1_out_2, controlled_buffer_1_out}), .in1(ALUout), .out(multiplexer_1_out),
    .sel(RegSrc));
  Register R0 (.D(multiplexer_1_out), .en(demultiplexer_1_out0), .Q(R0_q), .clk(clk), .clr(reset));
  Demultiplexer #(.select(2)) demultiplexer_1 (
    .out0(demultiplexer_1_out0), .out1(demultiplexer_1_out1), .out2(demultiplexer_1_out2),
    .out3(demultiplexer_1_out3), .in(Load_Register), .sel(Select_register));
  assign {controlled_buffer_1_out_2, controlled_buffer_1_out} = Store ? multiplexer_2_out : 8'bz;  // Controlled_Buffer controlled_buffer_1
  Multiplexer #(.width(8)) multiplexer_2 (.in0(value), .in1(Rstr), .out(multiplexer_2_out), .sel(Store_from_RA));
  Register R1 (.D(multiplexer_1_out), .en(demultiplexer_1_out1), .Q(R1_q), .clk(clk), .clr(reset));
  Register R2 (.D(multiplexer_1_out), .en(demultiplexer_1_out2), .Q(R2_q), .clk(clk), .clr(reset));
  RAM #(.asyncread("true"), .databus("bidir")) ram_1 (
    .addr(Mem_Address), .we(Store), .oe(not_1_out), .clk(clk),
    .data({controlled_buffer_1_out_2, controlled_buffer_1_out}));
  not not_1 (not_1_out, Store);
  Register R3 (.D(multiplexer_1_out), .en(demultiplexer_1_out3), .Q(R3_q), .clk(clk), .clr(reset));
  Hex_Digit_Display hex_digit_display_1 (.value(controlled_buffer_1_out_2));  // open: dp
  Hex_Digit_Display hex_digit_display_2 (.value(controlled_buffer_1_out));  // open: dp
  Hex_Digit_Display hex_digit_display_3 (.value(Rstr[7:4]));  // open: dp
  Multiplexer #(.select(2), .width(8)) multiplexer_3 (
    .in0(R0_q), .in1(R1_q), .in2(R2_q), .in3(R3_q), .out(Rstr), .sel(RA));
  Hex_Digit_Display hex_digit_display_4 (.value(multiplexer_4_out_2));  // open: dp
  Multiplexer #(.select(2), .width(8)) multiplexer_4 (
    .in0(R0_q), .in1(R1_q), .in2(R2_q), .in3(R3_q), .out({multiplexer_4_out_2, multiplexer_4_out}), .sel(RB));
  Hex_Digit_Display hex_digit_display_5 (.value(Rstr[3:0]));  // open: dp
  Hex_Digit_Display hex_digit_display_6 (.value(multiplexer_4_out));  // open: dp
  Hex_Digit_Display hex_digit_display_7 (.value(ALUout[7:4]));  // open: dp
  ALU alu_1 (.out_4(ALUout), .A(Rstr), .B({multiplexer_4_out_2, multiplexer_4_out}), .Instruction(Instruction));
  Clock clock_1 (.out(clk));
  Button button_1 (.out(reset));
  Hex_Digit_Display hex_digit_display_8 (.value(ALUout[3:0]));  // open: dp

  // Other names for the same wires on the sheet: Ins[3:0] = Instruction

  // Notes on the sheet:
  //   Preprost model CPE s krmilnimi signali
  //   Avtor: Filip Brajčič (2022)
endmodule

module Partial_Adder (
  input  A,
  input  B,
  output Carry,
  output Result
);

  wire and_1_out, and_2_out, not_1_out, not_2_out;

  and and_1 (and_1_out, A, not_1_out);
  not not_1 (not_1_out, B);
  and and_2 (and_2_out, B, not_2_out);
  not not_2 (not_2_out, A);
  and and_3 (Carry, A, B);
  or or_1 (Result, and_1_out, and_2_out);

  // Notes on the sheet:
  //   Delni seštevalnik
endmodule

module Adder (
  input  A,
  input  B,
  input  CarryIN,
  output Result,
  output CarryOUT
);

  wire partial_adder_1_carry, partial_adder_1_result, partial_adder_2_carry;

  Partial_Adder partial_adder_1 (.Carry(partial_adder_1_carry), .Result(partial_adder_1_result), .B(B), .A(A));
  Partial_Adder partial_adder_2 (
    .Carry(partial_adder_2_carry), .Result(Result), .B(CarryIN), .A(partial_adder_1_result));
  or or_1 (CarryOUT, partial_adder_2_carry, partial_adder_1_carry);

  // Notes on the sheet:
  //   Polni seštevalnik
endmodule

module L_8b_add_sub (
  input  [7:0] A,
  input  [7:0] B,
  input  L_1cabac28,
  output [7:0] Output,
  output Carry
);

  wire adder_2_carryout, adder_3_carryout, adder_4_carryout, adder_5_carryout, adder_6_carryout,
       adder_7_carryout, adder_8_carryout, xor_1_out, xor_2_out, xor_3_out, xor_4_out, xor_5_out, xor_6_out,
       xor_7_out, xor_8_out;

  xor xor_1 (xor_1_out, B[7], L_1cabac28);
  Adder adder_1 (.Result(Output[7]), .CarryOUT(Carry), .A(A[7]), .B(xor_1_out), .CarryIN(adder_2_carryout));
  xor xor_2 (xor_2_out, B[6], L_1cabac28);
  Adder adder_2 (.Result(Output[6]), .CarryOUT(adder_2_carryout), .A(A[6]), .B(xor_2_out), .CarryIN(adder_3_carryout));
  xor xor_3 (xor_3_out, B[5], L_1cabac28);
  Adder adder_3 (.Result(Output[5]), .CarryOUT(adder_3_carryout), .A(A[5]), .B(xor_3_out), .CarryIN(adder_4_carryout));
  xor xor_4 (xor_4_out, B[4], L_1cabac28);
  xor xor_5 (xor_5_out, B[3], L_1cabac28);
  Adder adder_4 (.Result(Output[4]), .CarryOUT(adder_4_carryout), .A(A[4]), .B(xor_4_out), .CarryIN(adder_5_carryout));
  Adder adder_5 (.Result(Output[3]), .CarryOUT(adder_5_carryout), .A(A[3]), .B(xor_5_out), .CarryIN(adder_6_carryout));
  xor xor_6 (xor_6_out, B[2], L_1cabac28);
  Adder adder_6 (.Result(Output[2]), .CarryOUT(adder_6_carryout), .A(A[2]), .B(xor_6_out), .CarryIN(adder_7_carryout));
  xor xor_7 (xor_7_out, B[1], L_1cabac28);
  Adder adder_7 (.Result(Output[1]), .CarryOUT(adder_7_carryout), .A(A[1]), .B(xor_7_out), .CarryIN(adder_8_carryout));
  xor xor_8 (xor_8_out, B[0], L_1cabac28);
  Adder adder_8 (.Result(Output[0]), .CarryOUT(adder_8_carryout), .A(A[0]), .B(xor_8_out), .CarryIN(L_1cabac28));

  // Other names for the same wires on the sheet: R[7:0] = Output

  // Notes on the sheet:
  //   Seštevalnik / Odštevalnik
endmodule

module ALU (
  input  [3:0] Instruction,
  input  [7:0] A,
  input  [7:0] B,
  output [7:0] out_4
);

  wire [7:0] and_1_out, l_8b_add_sub_1_output, multiplier_1_out, not_1_out, or_1_out;

  L_8b_add_sub l_8b_add_sub_1 (
    .Output(l_8b_add_sub_1_output), .A(A), .B(B), .L_1cabac28(Instruction[0]));  // open: Carry
  Multiplier multiplier_1 (.a(A), .b(B), .out(multiplier_1_out));  // open: cin, cout
  assign and_1_out = A & B;  // AND_Gate and_1, 8 bits wide
  assign or_1_out = A | B;  // OR_Gate or_1, 8 bits wide
  assign not_1_out = ~A;  // NOT_Gate not_1, 8 bits wide
  Multiplexer #(.enable("true"), .select(3), .width(8)) multiplexer_1 (
    .in0(l_8b_add_sub_1_output), .in1(multiplier_1_out), .in2(and_1_out), .in3(or_1_out), .in4(not_1_out),
    .out(out_4), .sel(Instruction[3:1]));  // open: in5, in6, in7, en
endmodule
