// Logisim project RA03_RAM_pomnilnik_demo_EVO.circ as structural Verilog: 1 circuit, main circuit main
module main (
  input  [15:0] Address,
  input  [7:0] Write_Register,
  input  Write_Read,
  output [7:0] Read_Register
);

  wire CLK_out, not_1_out;

  // Probe on Address
  Clock CLK (.out(CLK_out));
  // Probe on Read_Register
  // Probe on Write_Register
  assign Read_Register = Write_Read ? Write_Register : 8'bz;  // Controlled_Buffer controlled_buffer_1
  Hex_Digit_Display hex_digit_display_1 (.value(Address[15:12]));  // open: dp
  not not_1 (not_1_out, Write_Read);
  // Probe on Read_Register
  Hex_Digit_Display hex_digit_display_2 (.value(Address[11:8]));  // open: dp
  Hex_Digit_Display hex_digit_display_3 (.value(Address[7:4]));  // open: dp
  Hex_Digit_Display hex_digit_display_4 (.value(Address[3:0]));  // open: dp
  RAM #(.addrWidth(16), .databus("bidir"), .\type ("nonvolatile")) ram_1 (
    .addr(Address), .we(Write_Read), .oe(not_1_out), .clk(CLK_out), .data(Read_Register));
  Hex_Digit_Display hex_digit_display_5 (.value(Read_Register[7:4]));  // open: dp
  Hex_Digit_Display hex_digit_display_6 (.value(Read_Register[3:0]));  // open: dp

  // Notes on the sheet:
  //   Branje : - nastavi naslov  (Adress Bus)
  //   - Out_Enable = 1
  //   - Write_Read = 0
  //   - CLK: 1 cikel (dva klika)
  //   CPE
  //   Branje: 0
  //   Pisanje: 1
  //   A0
  //   A15
  //   Primer delovanja pomnilnika RAM
  //   Pisanje : - nastavi naslov (Adress Bus)
  //   - Out_Enable = 0
  //   - Write_Read = 1
  //   - Write_Data = podatek za vpis
  //   - CLK: 1 cikel (dva klika)
  //   Address Bus
  //   Control Bus
  //   Data Bus
  //   D0
  //   D7
  //   Pomnilnik
endmodule
