// Logisim project RA05_Univerzalni_Sestevalnik_4bitni.circ as structural Verilog: 2 circuits, main circuit main
module main (
  input  [3:0] in_1,
  input  [3:0] in_2,
  input  M,
  output C_ARM9,
  output prenos,
  output preliv,
  output [3:0] out_7
);

  wire fulladder_2_co, fulladder_3_co, fulladder_4_co;
  wire [3:0] adder_1_out, xor_6_out;

  // Probe on in_1
  // Probe on in_1
  xor xor_1 (prenos, M, C_ARM9);
  xor xor_2 (preliv, C_ARM9, fulladder_2_co);
  xor xor_3 (xor_6_out[3], in_2[3], M);
  FullAdder fulladder_1 (.A(xor_6_out[3]), .B(in_1[3]), .Ci(fulladder_2_co), .Co(C_ARM9), .S(out_7[3]));
  FullAdder fulladder_2 (.A(xor_6_out[2]), .B(in_1[2]), .Ci(fulladder_3_co), .Co(fulladder_2_co), .S(out_7[2]));
  // Probe on in_2
  // Probe on in_2
  xor xor_4 (xor_6_out[2], in_2[2], M);
  // Probe on out_7
  // Probe on out_7
  xor xor_5 (xor_6_out[1], in_2[1], M);
  FullAdder fulladder_3 (.A(xor_6_out[1]), .B(in_1[1]), .Ci(fulladder_4_co), .Co(fulladder_3_co), .S(out_7[1]));
  xor xor_6 (xor_6_out[0], in_2[0], M);
  FullAdder fulladder_4 (.A(xor_6_out[0]), .B(in_1[0]), .Ci(M), .Co(fulladder_4_co), .S(out_7[0]));
  // Probe on adder_1_out
  // Probe on adder_1_out
  Adder #(.width(4)) adder_1 (.a({3'b000, M}), .b(xor_6_out), .out(adder_1_out));  // open: cin, cout

  // Notes on the sheet:
  //   UnSigned
  //   Signed
  //   UnSigned
  //   Signed
  //   UnSigned
  //   Signed
  //   1 .. SUB
  //   0 .. ADD
  //   2. operand
  //   UnSigned
  //   Signed
endmodule

module FullAdder (
  input  A,
  input  B,
  input  Ci,
  output S,
  output Co
);

  wire and_1_out, and_2_out, xor_1_out;

  xor xor_1 (xor_1_out, A, B);
  xor xor_2 (S, xor_1_out, Ci);
  and and_1 (and_1_out, xor_1_out, Ci);
  or or_1 (Co, and_1_out, and_2_out);
  and and_2 (and_2_out, A, B);
endmodule
