// Logisim project RA05_Univerzalni_Sestevalnik_8bitni.circ as structural Verilog: 2 circuits, main circuit main
module main (
  input  [7:0] in_1,
  input  [7:0] in_2,
  input  M_1ADD_0SUB,
  output C_ARM9,
  output prenos,
  output preliv,
  output [7:0] out_7
);

  wire fulladder_2_co, fulladder_3_co, fulladder_4_co, fulladder_5_co, fulladder_6_co, fulladder_7_co,
       fulladder_8_co, xor_3_out, xor_4_out, xor_5_out, xor_6_out, xor_7_out, xor_8_out, xor_9_out,
       xor_10_out;

  xor xor_1 (prenos, M_1ADD_0SUB, C_ARM9);
  xor xor_2 (preliv, C_ARM9, fulladder_2_co);
  // Probe on in_1
  // Probe on in_1
  xor xor_3 (xor_3_out, in_2[7], M_1ADD_0SUB);
  FullAdder fulladder_1 (.Co(C_ARM9), .S(out_7[7]), .A(xor_3_out), .B(in_1[7]), .Ci(fulladder_2_co));
  xor xor_4 (xor_4_out, in_2[6], M_1ADD_0SUB);
  FullAdder fulladder_2 (.Co(fulladder_2_co), .S(out_7[6]), .A(xor_4_out), .B(in_1[6]), .Ci(fulladder_3_co));
  FullAdder fulladder_3 (.Co(fulladder_3_co), .S(out_7[5]), .A(xor_5_out), .B(in_1[5]), .Ci(fulladder_4_co));
  xor xor_5 (xor_5_out, in_2[5], M_1ADD_0SUB);
  xor xor_6 (xor_6_out, in_2[4], M_1ADD_0SUB);
  FullAdder fulladder_4 (.Co(fulladder_4_co), .S(out_7[4]), .A(xor_6_out), .B(in_1[4]), .Ci(fulladder_5_co));
  xor xor_7 (xor_7_out, in_2[3], M_1ADD_0SUB);
  FullAdder fulladder_5 (.Co(fulladder_5_co), .S(out_7[3]), .A(xor_7_out), .B(in_1[3]), .Ci(fulladder_6_co));
  xor xor_8 (xor_8_out, in_2[2], M_1ADD_0SUB);
  FullAdder fulladder_6 (.Co(fulladder_6_co), .S(out_7[2]), .A(xor_8_out), .B(in_1[2]), .Ci(fulladder_7_co));
  // Probe on out_7
  // Probe on out_7
  // Probe on in_2
  // Probe on in_2
  FullAdder fulladder_7 (.Co(fulladder_7_co), .S(out_7[1]), .A(xor_9_out), .B(in_1[1]), .Ci(fulladder_8_co));
  xor xor_9 (xor_9_out, in_2[1], M_1ADD_0SUB);
  xor xor_10 (xor_10_out, in_2[0], M_1ADD_0SUB);
  FullAdder fulladder_8 (.Co(fulladder_8_co), .S(out_7[0]), .A(xor_10_out), .B(in_1[0]), .Ci(M_1ADD_0SUB));

  // Notes on the sheet:
  //   UnSigned
  //   Signed
  //   UnSigned
  //   Signed
  //   UnSigned
  //   Signed
endmodule

module FullAdder (
  input  A,
  input  B,
  input  Ci,
  output S,
  output Co
);

  wire and_1_out, and_2_out, xor_1_out;

  xor xor_1 (xor_1_out, A, B);
  xor xor_2 (S, xor_1_out, Ci);
  and and_1 (and_1_out, xor_1_out, Ci);
  or or_1 (Co, and_1_out, and_2_out);
  and and_2 (and_2_out, A, B);
endmodule
