// Logisim project RA06_sestevalniki_1in2bit.circ as structural Verilog: 3 circuits, main circuit main
module main (
  input  A,
  input  [1:0] in_2,
  input  B,
  input  [1:0] in_4,
  input  Cin,
  output C,
  output S,
  output [1:0] Res,
  output Cout
);

  adder_1bit adder_1bit_1 (.A(A), .B(B), .Cin(Cin), .S(S), .Cout(Cout));
  LED led_1 (.in(S));
  LED led_2 (.in(Cout));
  adder_2bit adder_2bit_1 (.A(in_2), .B(in_4), .Cout(C), .SUM(Res));
  LED led_3 (.in(C));
  // Probe on Res

  // Notes on the sheet:
  //   1-bit adder
  //   2-bit adder
endmodule

module adder_1bit (
  input  A,
  input  B,
  input  Cin,
  output S,
  output Cout
);

  wire and_1_out, and_2_out, and_3_out, and_4_out, and_5_out, and_6_out, and_7_out, not_1_out, not_2_out,
       not_3_out, not_4_out, not_5_out, not_6_out;

  not not_1 (not_1_out, A);
  not not_2 (not_2_out, B);
  not not_3 (not_3_out, A);
  not not_4 (not_4_out, Cin);
  not not_5 (not_5_out, B);
  not not_6 (not_6_out, Cin);
  and and_1 (and_1_out, B, Cin);
  and and_2 (and_2_out, A, Cin);
  and and_3 (and_3_out, A, B);
  and and_4 (and_4_out, not_1_out, not_2_out, Cin);
  and and_5 (and_5_out, not_3_out, B, not_4_out);
  and and_6 (and_6_out, A, not_5_out, not_6_out);
  and and_7 (and_7_out, A, B, Cin);
  or or_1 (Cout, and_1_out, and_2_out, and_3_out);
  or or_2 (S, and_4_out, and_5_out, and_6_out, and_7_out);
endmodule

module adder_2bit (
  input  [1:0] A,
  input  [1:0] B,
  output Cout,
  output [1:0] SUM
);

  wire b0_cout;

  adder_1bit b1 (.A(A[1]), .B(B[1]), .Cin(b0_cout), .S(SUM[1]), .Cout(Cout));
  adder_1bit b0 (.A(A[0]), .B(B[0]), .Cin(1'b0), .S(SUM[0]), .Cout(b0_cout));

  // Notes on the sheet:
  //   Cout
endmodule
