// Logisim project RA06_stevec_3bit_down.circ as structural Verilog: 1 circuit, main circuit main
module main (
  output _4,
  output _2,
  output _1
);

  wire clock_1_out, d_ff_1_qn, d_ff_2_qn, d_ff_3_qn;

  Clock clock_1 (.out(clock_1_out));
  D_Flip_Flop d_ff_1 (.clk(clock_1_out), .D(d_ff_1_qn), .Q(_1), .Qn(d_ff_1_qn));  // open: preset, reset
  LedBar #(.matrixcols(3)) ledbar_1 (.led0(_4), .led1(_2), .led2(_1));
  D_Flip_Flop d_ff_2 (.clk(_1), .D(d_ff_2_qn), .Q(_2), .Qn(d_ff_2_qn));  // open: preset, reset
  Hex_Digit_Display hex_digit_display_1 (.value({1'b0, _4, _2, _1}));  // open: dp
  D_Flip_Flop d_ff_3 (.clk(_2), .D(d_ff_3_qn), .Q(_4), .Qn(d_ff_3_qn));  // open: preset, reset
endmodule
