// Logisim project RA09_Simple_Fully_Associative_Cache.circ as structural Verilog: 1 circuit, main circuit main
module main (
  input  [4:0] in_1,
  input  Manual,
  input  [2:0] \Št__blokov_tags ,
  input  V0,
  input  [2:0] in_5,
  input  V1,
  input  [2:0] in_7,
  input  V2,
  input  [2:0] in_9,
  input  V3,
  input  EN,
  output [7:0] out_12
);

  wire and_1_out, and_2_out, and_3_out, and_4_out, comparator_1_eq, comparator_2_eq, comparator_3_eq,
       comparator_4_eq, Korak_out, not_1_out, or_1_out, Reset_out;
  wire [1:0] priority_encoder_1_out;
  wire [3:0] Addr, counter_1_q;
  wire [4:0] Naslov;
  wire [7:0] counter_2_q, counter_3_q;
  wire [31:0] rom_1_data;

  Counter #(.max('hf), .width(4)) counter_1 (
    .count(EN), .Q(counter_1_q), .clk(Korak_out), .clr(Reset_out));  // open: load, D, carry, up
  Button Korak (.out(Korak_out));
  // Probe on \Št__blokov_tags 
  // Probe on in_5
  // Probe on in_7
  // Probe on in_9
  // Probe on Addr
  BitSelector #(.group(4), .width(64)) bitselector_1 (.in(64'h52ba932ba9), .out(Addr), .sel(counter_1_q));
  Button Reset (.out(Reset_out));
  Comparator #(.mode("unsigned"), .width(3)) comparator_1 (
    .a(\Št__blokov_tags ), .b(Naslov[4:2]), .eq(comparator_1_eq));  // open: gt, lt
  Comparator #(.mode("unsigned"), .width(3)) comparator_2 (
    .a(in_5), .b(Naslov[4:2]), .eq(comparator_2_eq));  // open: gt, lt
  Comparator #(.mode("unsigned"), .width(3)) comparator_3 (
    .a(in_7), .b(Naslov[4:2]), .eq(comparator_3_eq));  // open: gt, lt
  Comparator #(.mode("unsigned"), .width(3)) comparator_4 (
    .a(in_9), .b(Naslov[4:2]), .eq(comparator_4_eq));  // open: gt, lt
  // Probe on Naslov[4:2]
  // Probe on Naslov[4:2]
  and and_1 (and_1_out, comparator_1_eq, V0);
  LED led_1 (.in(and_1_out));
  and and_2 (and_2_out, comparator_2_eq, V1);
  LED led_2 (.in(and_2_out));
  and and_3 (and_3_out, comparator_3_eq, V2);
  LED led_3 (.in(and_3_out));
  and and_4 (and_4_out, comparator_4_eq, V3);
  LED led_4 (.in(and_4_out));
  Multiplexer #(.width(5)) multiplexer_1 (.in0({1'b0, Addr}), .in1(in_1), .out(Naslov), .sel(Manual));
  // Probe on Naslov
  // Probe on Naslov
  // Probe on priority_encoder_1_out
  Priority_Encoder #(.select(2)) priority_encoder_1 (
    .in0(and_1_out), .in1(and_2_out), .in2(and_3_out), .in3(and_4_out), .out(priority_encoder_1_out));  // open: gs, en_out, en_in
  or or_1 (or_1_out, and_1_out, and_2_out, and_3_out, and_4_out);
  ROM #(.addrWidth(2), .dataWidth(32)) rom_1 (.addr(priority_encoder_1_out), .data(rom_1_data));
  // Probe on Naslov[1:0]
  // Probe on Naslov[1:0]
  BitSelector #(.group(8), .width(32)) bitselector_2 (.in(rom_1_data), .out(out_12), .sel(Naslov[1:0]));
  // Probe on out_12
  // Probe on out_12
  // Probe on rom_1_data
  LED Hit (.in(or_1_out));
  LED Miss (.in(or_1_out));
  not not_1 (not_1_out, or_1_out);
  Counter counter_2 (.count(or_1_out), .Q(counter_2_q), .clk(Korak_out), .clr(Reset_out));  // open: load, D, carry, up
  Counter counter_3 (.count(not_1_out), .Q(counter_3_q), .clk(Korak_out), .clr(Reset_out));  // open: load, D, carry, up
  // Probe on counter_2_q
  // Probe on counter_3_q

  // Notes on the sheet:
  //   Št. Bloka #0
  //   Št. Bloka #1
  //   Št. Bloka #2
  //   Št. Bloka #3
  //   Generator zaporedja naslovov
  //   Kontrolni del (asociativni) 
  //   Primerjalniki
  //   Št. Bloka
  //   Nastavitve: Blok #0=2, Blok #1=0, V0=V1=1
  //   Naslov
  //   Zaporedje naslovov: 9, 10, 11, 2, 3, 9, 10, 11, 2, 5
  //   Naslov ujemanja
  //   Navodila: tipka Korak proži zaporedje naslovov, zadnji je zgrešitev
  //   contents of rom_1 (hex, n*v repeats v):
  //   6361fa4 74cb3112
  //   Pomnilniški del 
  //   Naslov znotraj bloka
  //   Vsebine blokov
  //   Izbran blok
  //   Vsebina pomn. besede
  //   Zadetki
  //   Zgrešitve
endmodule
