// Logisim project RA09_Simple_Virtual_Memory_With_Pages.circ as structural Verilog: 1 circuit, main circuit main
module main (
  input  [7:0] in_1,
  input  Manual,
  output [5:0] out_3,
  output [7:0] Vsebina_besede
);

  wire and_1_out, button_1_out, Reset_out;
  wire [4:0] PageNum;
  wire [7:0] bitselector_1_out, counter_1_q;
  wire [19:3] rom_1_data;
  wire [63:0] rom_2_data;

  // Probe on PageNum
  // Probe on PageNum
  ROM #(.addrWidth(5), .dataWidth(20)) rom_1 (.addr(PageNum), .data({rom_1_data, out_3[5:3]}));
  // Probe on {PageNum, out_3[2:0]}
  // Probe on {PageNum, out_3[2:0]}
  // Probe on out_3[2:0]
  // Probe on out_3[2:0]
  Button button_1 (.out(button_1_out));
  LED led_1 (.in(rom_1_data[16]));
  LED led_2 (.in(rom_1_data[12]));
  Counter counter_1 (.count(1'b1), .Q(counter_1_q), .clk(button_1_out), .clr(Reset_out));  // open: load, D, carry, up
  Button Reset (.out(Reset_out));
  // Probe on PageNum
  LED led_3 (.in(rom_1_data[4]));
  LedBar #(.matrixcols(3)) ledbar_1 (.led0(rom_1_data[10]), .led1(rom_1_data[9]), .led2(rom_1_data[8]));
  Multiplexer #(.width(8)) multiplexer_1 (.in0(counter_1_q), .in1(in_1), .out({PageNum, out_3[2:0]}), .sel(Manual));
  // Probe on {PageNum, out_3[2:0]}
  // Probe on out_3[5:3]
  and and_1 (and_1_out, rom_1_data[12], rom_1_data[16]);
  ROM #(.addrWidth(3), .dataWidth(64)) rom_2 (.addr(out_3[5:3]), .data(rom_2_data));
  // Probe on out_3
  // Probe on out_3[2:0]
  BitSelector #(.group(8), .width(64)) bitselector_1 (.in(rom_2_data), .out(bitselector_1_out), .sel(out_3[2:0]));
  // Probe on bitselector_1_out
  // Probe on bitselector_1_out
  assign Vsebina_besede = and_1_out ? bitselector_1_out : 8'bz;  // Controlled_Buffer controlled_buffer_1
  // Probe on rom_2_data
  // Probe on Vsebina_besede
  // Probe on Vsebina_besede
  LED Hit (.in(and_1_out));
  LED Page_Fault (.in(and_1_out));
  ROM #(.addrWidth(5), .dataWidth(64)) rom_3 ();  // open: addr, data
  // Probe on nothing

  // Other names for the same wires on the sheet: Offset[2:0] = out_3[2:0]

  // Notes on the sheet:
  //   Navidezni pomnilnik - model
  //   Program zajema 4 strani (0,1,2,3),
  //   ki so v GP v okvirjih 0,5,3,2
  //   contents of rom_1 (hex, n*v repeats v):
  //   11700 11705 11703 11702
  //   Navidezni naslov
  //   Tabela strani
  //   Deskriptor - polja
  //   V | P | RWX | C | FN
  //   V
  //   P
  //   V (Valid), P (Present), RWX (Read,Write,eXecute), C (Change), FN (Frame Number)     
  //   Št. strani
  //   Deskriptor
  //   RWX
  //   C
  //   Navodila: tipka proži zaporedne naslove od 0 naprej. Bajti v pomnilniku so 0x, 1x, 2x, 3x (x=1..8), naslov 32 sproži Page_Fault
  //   Navidezni naslov
  //   8 bitni navidezni naslov
  //   5b št. strani | 3b naslov znotraj strani
  //   Številka okvirja (FN)
  //   contents of rom_2 (hex, n*v repeats v):
  //   807060504030201 0 3837363534333231 2827262524232221 0 1817161514131211
  //   Glavni pomnilnik
  //   Fizični naslov
  //   Naslov znotraj strani
  //   Okvirji strani
  //   3b št. okvirja | 3b odmik znotraj strani
  //   GP: 8 okvirjev strani po 8 besed-bajtov
  //   6 bitni (8 okvirjev strani po 8 besed-bajtov)
  //   contents of rom_3 (hex, n*v repeats v):
  //   807060504030201 1817161514131211 2827262524232221 3837363534333231
  //   NP: 32 strani po 8 besed-bajtov
endmodule
