// Logisim project Mikro MiMo - Simple CPU Model_v0.circ as structural Verilog: 10 circuits, main circuit ALU
// address
module MikroMiMo (
  input  [15:0] PC,
  input  Address,
  input  ReadWrite,
  input  RegWrite,
  input  [1:0] RegSrc,
  input  [1:0] aluop,
  input  ADR,
  input  irload
);

  wire and_1_out, and_2_out, c, CLK, Itype, n, not_1_out, Phase, reset, z;
  wire [2:0] InstrTyp;
  wire [3:0] icycles, opcode, Rdsel, Rmsel, Rnsel, showhexa32_1_out_2, showhexa32_1_out_3,
       showhexa32_1_out_4, showhexa32_1_out_5, showhexa32_1_out_6, showhexa32_1_out_7, showhexa32_1_out_8,
       showhexa32_1_out_9, showhexa_1_digit, showhexa_1_out_2, showhexa_1_out_3, showhexa_1_out_5;
  wire [15:0] address_t, cmds, cycles;
  wire [31:0] aluout, data, ImmVal, instructionreg_1_instruction_register_content, multiplexer_2_out,
       multiplexer_3_out, multiplexer_4_out, pc32, Rd, registerfile_1_r0, registerfile_1_r1,
       registerfile_1_r2, registerfile_1_r3, Rm, Rn;

  Button u_Reset (.out(reset));
  // Probe on InstrTyp
  Registerfile registerfile_1 (
    .Rdsel(Rdsel), .Rnsel(Rnsel), .Rmsel(Rmsel), .regval(multiplexer_2_out), .clock(CLK), .Reset(reset),
    .dwrite(RegWrite), .r0(registerfile_1_r0), .r1(registerfile_1_r1), .r2(registerfile_1_r2),
    .r3(registerfile_1_r3), .Regn(Rn), .Regm(Rm), .Regd(Rd));
  ALUSimple alusimple_1 (
    .A(multiplexer_3_out), .B(multiplexer_4_out), .aluop(aluop), .Result(aluout), .Carry(c), .Negative(n),
    .Zero(z));
  LED Carry (.in(c));
  LED Zero (.in(z));
  // Probe on PC
  Multiplexer #(.width(16)) multiplexer_1 (.in0(PC), .in1(Rn[15:0]), .out(address_t), .sel(Address));
  // Probe on Rn[15:0]
  InstructionReg instructionreg_1 (
    .reset(reset), .irload(irload), .instruction(data), .clock(CLK),
    .Instruction_register_Content(instructionreg_1_instruction_register_content), .ImmVal32b(ImmVal),
    .Rm(Rmsel), .Rd(Rdsel), .Rn(Rnsel), .opcode(opcode), .InstrType(InstrTyp), .I_Type(Itype));
  // Probe on opcode
  // Probe on Itype
  // Probe on Rdsel
  // Probe on registerfile_1_r0
  // Probe on registerfile_1_r1
  // Probe on registerfile_1_r2
  // Probe on registerfile_1_r3
  // Probe on multiplexer_3_out
  // Probe on multiplexer_4_out
  // Probe on aluout
  LED Neg (.in(n));
  Clock SysClk (.out(CLK));
  assign pc32 = {{16{1'b0}}, PC};  // Bit_Extender bit_extender_1
  // Probe on address_t
  // Probe on instructionreg_1_instruction_register_content
  // Probe on Rnsel
  // Probe on Rmsel
  // Probe on multiplexer_2_out
  Multiplexer #(.select(2), .width(32)) multiplexer_2 (
    .in0(data), .in1(aluout), .in2(ImmVal), .out(multiplexer_2_out), .sel(RegSrc));  // open: in3
  // Probe on Rd
  // Probe on Rm
  Multiplexer #(.width(32)) multiplexer_3 (.in0(Rn), .in1(pc32), .out(multiplexer_3_out), .sel(ADR));
  Multiplexer #(.width(32)) multiplexer_4 (.in0(Rm), .in1(ImmVal), .out(multiplexer_4_out), .sel(ADR));
  assign data = ReadWrite ? Rd : 32'bz;  // Controlled_Buffer controlled_buffer_1
  Hex_Digit_Display hex_digit_display_1 (.value(showhexa32_1_out_2));  // open: dp
  Hex_Digit_Display hex_digit_display_2 (.value(showhexa32_1_out_3));  // open: dp
  Hex_Digit_Display hex_digit_display_3 (.value(showhexa_1_out_2));  // open: dp
  ShowHexa showhexa_1 (
    .Data(address_t), .Digit(showhexa_1_digit), .out_5(showhexa_1_out_5), .out_2(showhexa_1_out_2),
    .out_3(showhexa_1_out_3));
  Hex_Digit_Display hex_digit_display_4 (.value(showhexa32_1_out_4));  // open: dp
  ShowHexa32 showhexa32_1 (
    .Data(data), .out_3(showhexa32_1_out_3), .out_4(showhexa32_1_out_4), .out_5(showhexa32_1_out_5),
    .out_6(showhexa32_1_out_6), .out_7(showhexa32_1_out_7), .out_8(showhexa32_1_out_8),
    .out_9(showhexa32_1_out_9), .out_2(showhexa32_1_out_2));
  Hex_Digit_Display hex_digit_display_5 (.value(showhexa_1_out_3));  // open: dp
  Hex_Digit_Display hex_digit_display_6 (.value(showhexa_1_digit));  // open: dp
  Hex_Digit_Display hex_digit_display_7 (.value(showhexa32_1_out_5));  // open: dp
  Hex_Digit_Display hex_digit_display_8 (.value(showhexa32_1_out_6));  // open: dp
  LED led_1 (.in(ReadWrite));
  Hex_Digit_Display hex_digit_display_9 (.value(showhexa_1_out_5));  // open: dp
  Hex_Digit_Display hex_digit_display_10 (.value(showhexa32_1_out_7));  // open: dp
  LED led_2 (.in(ReadWrite));
  // Probe on 1'b1
  // Probe on PC
  Hex_Digit_Display hex_digit_display_11 (.value(showhexa32_1_out_8));  // open: dp
  Hex_Digit_Display hex_digit_display_12 (.value(showhexa32_1_out_9));  // open: dp
  // Probe on address_t
  not not_1 (not_1_out, ReadWrite);
  LED led_3 (.in(Address));
  // Probe on data
  // Probe on Phase
  LED led_4 (.in(Phase));
  RAM #(.addrWidth(16), .asyncread("true"), .dataWidth(32), .databus("bidir"), .\type ("nonvolatile")) ram_1 (
    .addr(address_t), .we(and_1_out), .oe(and_2_out), .clk(CLK), .data(data));
  and and_1 (and_1_out, 1'b1, ReadWrite);
  and and_2 (and_2_out, 1'b1, not_1_out);
  LED led_5 (.in(ReadWrite));
  // Probe on InstrTyp
  LED led_6 (.in(Phase));
  LED led_7 (.in(RegWrite));
  // Probe on opcode
  // Probe on Rdsel
  // Probe on ReadWrite
  LED led_8 (.in(ReadWrite));
  // Probe on RegSrc
  // Probe on Rnsel
  // Probe on Rmsel
  LED led_9 (.in(ReadWrite));
  // Probe on aluop
  LED led_10 (.in(ADR));
  // Probe on ImmVal
  LED led_11 (.in(irload));
  Counter #(.max('h1), .width(1)) counter_1 (
    .Q(Phase), .up(1'b1), .clk(CLK), .clr(reset));  // open: load, D, count, carry
  LED u_C (.in(c));
  LED u_Z (.in(z));
  LED u_N (.in(n));
  Counters counters_1 (
    .new_ucounter(Phase), .reset(reset), .clock(CLK), .cmds(cmds), .cycles(cycles), .icycles(icycles));
  // Probe on cycles
  // Probe on cmds

  // Other names for the same wires on the sheet: addrsel = Address; dwrite = RegWrite

  // Notes on the sheet:
  //   PC: initial=0x20
  //   ALU
  //   Rd
  //   Registers
  //   Rn
  //   Rm
  //   Mikro MiMo - Simple CPU Model
  //   Pseudo instr. ADR R0,Address -> SUB R0, PC, #imm
  //   Address BUS
  //   Data BUS
  //   Control BUS
  //   Read
  //   Write
  //   PC
  //   v0 EVO
  //   Address
  //   0 PC
  //   1 Rn
  //   Exec STR:     Address=1, ReadWrite=1
  //   Data
  //   Fetch
  //   1 Write
  //   Exec LDR:      Address=1,                  RegWrite=1, RegSrc=0
  //   Exec ADD:                                          RegWrite=1, RegSrc=1, aluop=0
  //   CPU Info
  //   Execute
  //   Control Unit - signals
  //   1 Write Rd
  //   Fetch (PC+4):      Address=0, ReadWrite=0,              RegSrc=0,                        irload=1
  //   Exec ADR:                                          RegWrite=1, RegSrc=1, aluop=2,ADR=1
  //   Control Unit: How to Fetch and Execute
  //   Instruction:
  //   Rd
  //   Rn
  //   Read
  //   RAM
  //   0 DBus
  //   1 ALU
  //   2 IMM
  //   Rm
  //   Write
  //   0 ADD
  //   2 SUB
  //   1 ADR instr.
  //   immed 
  //   1 Write
  //   Phase counter
  //   Flags
endmodule

// IR
module InstructionReg (
  input  [31:0] instruction,
  input  reset,
  input  irload,
  input  clock,
  output [3:0] Rm,
  output [31:0] ImmVal32b,
  output [3:0] Rd,
  output [3:0] Rn,
  output [3:0] opcode,
  output I_Type,
  output [2:0] InstrType,
  output [31:0] Instruction_register_Content
);

  Register #(.width(32)) register_1 (
    .D(instruction), .en(irload),
    .Q({Instruction_register_Content[31:28], InstrType[2:1], I_Type, Instruction_register_Content[24:0]}),
    .clk(clock), .clr(reset));
  assign ImmVal32b = {{24{1'b0}}, Instruction_register_Content[7:0]};  // Bit_Extender bit_extender_1

  assign InstrType[0] = I_Type;
  assign Instruction_register_Content[27:25] = {InstrType[2:1], I_Type};
  assign opcode = Instruction_register_Content[24:21];
  assign Rd = Instruction_register_Content[15:12];
  assign Rm = Instruction_register_Content[3:0];
  assign Rn = Instruction_register_Content[19:16];

  // Notes on the sheet:
  //   ARM IR Logic
  //   Shift
  //   Sflags
  //   Condition
endmodule

module Registerfile (
  input  [31:0] regval,
  input  Reset,
  input  [3:0] Rdsel,
  input  [3:0] Rnsel,
  input  [3:0] Rmsel,
  input  dwrite,
  input  clock,
  output [31:0] r0,
  output [31:0] r1,
  output [31:0] r2,
  output [31:0] r3,
  output [31:0] Regn,
  output [31:0] Regm,
  output [31:0] Regd
);

  wire demultiplexer_1_out0, demultiplexer_1_out1, demultiplexer_1_out2, demultiplexer_1_out3;

  // Probe on regval
  // Probe on regval
  Demultiplexer #(.select(4)) demultiplexer_1 (
    .out0(demultiplexer_1_out0), .out1(demultiplexer_1_out1), .out2(demultiplexer_1_out2),
    .out3(demultiplexer_1_out3), .in(dwrite), .sel(Rdsel));  // open: out4, out5, out6, out7, out8, out9, out10, out11, out12, out13, out14, out15
  // Probe on Rnsel
  // Probe on Rmsel
  Register #(.width(32)) register_1 (.D(regval), .en(demultiplexer_1_out0), .Q(r0), .clk(clock), .clr(Reset));
  Register #(.width(32)) register_2 (.D(regval), .en(demultiplexer_1_out1), .Q(r1), .clk(clock), .clr(Reset));
  Register #(.width(32)) register_3 (.D(regval), .en(demultiplexer_1_out2), .Q(r2), .clk(clock), .clr(Reset));
  Register #(.width(32)) register_4 (.D(regval), .en(demultiplexer_1_out3), .Q(r3), .clk(clock), .clr(Reset));
  Multiplexer #(.select(4), .width(32)) multiplexer_1 (
    .in0(r0), .in1(r1), .in2(r2), .in3(r3), .out(Regn), .sel(Rnsel));  // open: in4, in5, in6, in7, in8, in9, in10, in11, in12, in13, in14, in15
  // Probe on Regn
  Multiplexer #(.select(4), .width(32)) multiplexer_2 (
    .in0(r0), .in1(r1), .in2(r2), .in3(r3), .out(Regm), .sel(Rmsel));  // open: in4, in5, in6, in7, in8, in9, in10, in11, in12, in13, in14, in15
  // Probe on Regm
  Multiplexer #(.select(4), .width(32)) multiplexer_3 (
    .in0(r0), .in1(r1), .in2(r2), .in3(r3), .out(Regd), .sel(Rdsel));  // open: in4, in5, in6, in7, in8, in9, in10, in11, in12, in13, in14, in15
  // Probe on Regd
  // Probe on r0
  // Probe on r0
  // Probe on r1
  // Probe on r1
  // Probe on r2
  // Probe on r2
  // Probe on r3
  // Probe on r3

  // Notes on the sheet:
  //   Register File
  //   Rn
  //   Rm
  //   Rd
  //   R0
  //   R1
  //   R2
  //   R3
endmodule

module ALU (
  input  [31:0] A,
  input  [31:0] B,
  input  [3:0] aluop,
  output Carry,
  output Zero,
  output Negative,
  output [31:0] Result
);

  wire adder_1_cout, or_2_out, subtractor_1_bout;
  wire [31:0] adder_1_out, and_1_out, divider_1_out, divider_1_rem, multiplier_1_out, nand_1_out, nor_1_out,
       not_1_out, or_1_out, shifter_1_out, shifter_2_out, shifter_3_out, shifter_4_out, shifter_5_out,
       subtractor_1_out, xor_1_out;

  Adder #(.width(32)) adder_1 (.a(A), .b(B), .out(adder_1_out), .cin(1'b0), .cout(adder_1_cout));
  Subtractor #(.width(32)) subtractor_1 (.a(A), .b(B), .out(subtractor_1_out), .bin(1'b0), .bout(subtractor_1_bout));
  Multiplier #(.width(32)) multiplier_1 (.a(A), .b(B), .out(multiplier_1_out), .cin({32{1'b0}}));  // open: cout
  Divider #(.width(32)) divider_1 (.a(A), .b(B), .out(divider_1_out), .upper({32{1'b0}}), .rem(divider_1_rem));
  assign and_1_out = A & B;  // AND_Gate and_1, 32 bits wide
  assign or_1_out = A | B;  // OR_Gate or_1, 32 bits wide
  assign xor_1_out = A ^ B;  // XOR_Gate xor_1, 32 bits wide
  assign nand_1_out = ~(A & B);  // NAND_Gate nand_1, 32 bits wide
  assign nor_1_out = ~(A | B);  // NOR_Gate nor_1, 32 bits wide
  assign not_1_out = ~A;  // NOT_Gate not_1, 32 bits wide
  Shifter #(.width(32)) shifter_1 (.in(A), .\dist (B[4:0]), .out(shifter_1_out));
  Shifter #(.shift("lr"), .width(32)) shifter_2 (.in(A), .\dist (B[4:0]), .out(shifter_2_out));
  Shifter #(.shift("ar"), .width(32)) shifter_3 (.in(A), .\dist (B[4:0]), .out(shifter_3_out));
  Shifter #(.shift("rl"), .width(32)) shifter_4 (.in(A), .\dist (B[4:0]), .out(shifter_4_out));
  Shifter #(.shift("rr"), .width(32)) shifter_5 (.in(A), .\dist (B[4:0]), .out(shifter_5_out));
  Multiplexer #(.select(4), .width(32)) multiplexer_1 (
    .in0(adder_1_out), .in1(subtractor_1_out), .in2(multiplier_1_out), .in3(divider_1_out),
    .in4(divider_1_rem), .in5(and_1_out), .in6(or_1_out), .in7(xor_1_out), .in8(nand_1_out), .in9(nor_1_out),
    .in10(not_1_out), .in11(shifter_1_out), .in12(shifter_2_out), .in13(shifter_3_out), .in14(shifter_4_out),
    .in15(shifter_5_out), .out({Negative, Result[30:0]}), .sel(aluop));
  Multiplexer #(.select(4)) multiplexer_2 (
    .in0(adder_1_cout), .in1(subtractor_1_bout), .in2(1'b0), .in3(1'b0), .in4(1'b0), .in5(1'b0), .in6(1'b0),
    .in7(1'b0), .in8(1'b0), .in9(1'b0), .in10(1'b0), .in11(1'b0), .in12(1'b0), .in13(1'b0), .in14(1'b0),
    .in15(1'b0), .out(Carry), .sel(aluop));
  or or_2 (or_2_out, Result[0], Result[1], Result[2], Result[3], Result[4], Result[5], Result[6], Result[7], Result[8], Result[9], Result[10], Result[11], Result[12], Result[13], Result[14], Result[15], Result[17], Result[18], Result[19], Result[20], Result[21], Result[22], Result[23], Result[24], Result[25], Result[26], Result[27], Result[28], Result[29], Result[30], Negative, Result[16]);
  not not_2 (Zero, or_2_out);

  assign Result[31] = Negative;

  // Notes on the sheet:
  //   32-bit ALU
endmodule

module PC (
  input  [15:0] imreg,
  input  pcload,
  input  clock,
  input  reset,
  input  pcsel,
  output [15:0] pcout
);

  wire [15:0] adder_1_out, multiplexer_1_out;

  Adder #(.width(16)) adder_1 (.a(pcout), .b(16'h1), .out(adder_1_out));  // open: cin, cout
  Multiplexer #(.width(16)) multiplexer_1 (.in0(adder_1_out), .in1(imreg), .out(multiplexer_1_out), .sel(pcsel));
  Register #(.width(16)) register_1 (.D(multiplexer_1_out), .en(pcload), .Q(pcout), .clk(clock), .clr(reset));

  // Notes on the sheet:
  //   PC Logic
endmodule

module ShowHexa (
  input  [15:0] Data,
  output [3:0] out_2,
  output [3:0] out_3,
  output [3:0] Digit,
  output [3:0] out_5
);


  assign Digit = Data[7:4];
  assign out_2 = Data[15:12];
  assign out_3 = Data[11:8];
  assign out_5 = Data[3:0];
endmodule

module Counters (
  input  new_ucounter,
  input  reset,
  input  clock,
  output [15:0] cycles,
  output [3:0] icycles,
  output [15:0] cmds
);

  wire not_1_out;

  not not_1 (not_1_out, new_ucounter);
  Counter #(.max('hffff), .width(16)) counter_1 (
    .Q(cycles), .clk(clock), .clr(reset));  // open: load, D, count, carry, up
  Counter #(.max('hf), .width(4)) counter_2 (
    .load(not_1_out), .D(4'b0000), .Q(icycles), .clk(clock), .clr(reset));  // open: count, carry, up
  Counter #(.max('hffff), .width(16)) counter_3 (
    .count(not_1_out), .Q(cmds), .clk(clock), .clr(reset));  // open: load, D, carry, up
  // Probe on cycles
  // Probe on icycles
  // Probe on cmds

  // Notes on the sheet:
  //   Counts the number of clock cycles
  //   since the start.
  //   Counts the number of clock cycles
  //   since the start of current instruction.
  //   Counts the number of instructions
  //   since the start.
  //   Cycle/Cmds Counters
endmodule

module DebugUnit (
  input  reset,
  input  \continue ,
  input  clock,
  input  [15:0] pcreg,
  input  [15:0] break_addr,
  input  break_on_addr,
  input  ucounter,
  input  break_on_instr,
  input  break_on_cycle,
  output clock_out
);

  wire and_1_out, and_2_out, and_3_out, nor_1_out, nor_2_out, not_1_out, or_1_out, shift_register_1_out,
       shift_register_1_q0;
  wire [15:0] xor_1_out;

  Shift_Register #(.length(2), .trigger("falling")) shift_register_1 (
    .in(\continue ), .clk(clock), .out(shift_register_1_out), .clr(reset), .q0(shift_register_1_q0));  // open: shift, load, d0, d1, q1
  assign xor_1_out = pcreg ^ break_addr;  // XOR_Gate xor_1, 16 bits wide
  LED Addr (.in(break_on_addr));
  not not_1 (not_1_out, ucounter);
  and and_1 (and_1_out, ~shift_register_1_out, shift_register_1_q0);  // AND_Gate
  nor nor_1 (nor_1_out, xor_1_out[15], xor_1_out[14], xor_1_out[13], xor_1_out[12], xor_1_out[11], xor_1_out[10], xor_1_out[9], xor_1_out[8], xor_1_out[6], xor_1_out[5], xor_1_out[4], xor_1_out[3], xor_1_out[2], xor_1_out[1], xor_1_out[0], xor_1_out[7]);
  and and_2 (and_2_out, nor_1_out, break_on_addr, not_1_out);
  and and_3 (and_3_out, not_1_out, break_on_instr);
  LED Instr (.in(break_on_instr));
  LED Cycle (.in(break_on_cycle));
  nor nor_2 (nor_2_out, and_2_out, and_3_out, break_on_cycle);
  or or_1 (or_1_out, and_1_out, nor_2_out);
  LED Pass (.in(or_1_out));
  and and_4 (clock_out, clock, or_1_out);

  // Notes on the sheet:
  //   Breaks on PC = break_addr
  //   Breaks on each new instruction
  //   Breaks on each clock pulse
  //   Makes sure the 'continue' button only
  //   lets through 1 clock pulse, until you let go
  //   and press it again.
  //   Outputs 1 only on first cycle (shift bits are unequal).
  //   Debug Unit
  //   PC = break_addr?
endmodule

module ShowHexa32 (
  input  [31:0] Data,
  output [3:0] out_2,
  output [3:0] out_3,
  output [3:0] out_4,
  output [3:0] out_5,
  output [3:0] out_6,
  output [3:0] out_7,
  output [3:0] out_8,
  output [3:0] out_9
);


  assign out_2 = Data[31:28];
  assign out_3 = Data[27:24];
  assign out_4 = Data[23:20];
  assign out_5 = Data[19:16];
  assign out_6 = Data[15:12];
  assign out_7 = Data[11:8];
  assign out_8 = Data[7:4];
  assign out_9 = Data[3:0];

  // Notes on the sheet:
  //   Digits
endmodule

module ALUSimple (
  input  [31:0] A,
  input  [31:0] B,
  input  [1:0] aluop,
  output Carry,
  output Zero,
  output Negative,
  output [31:0] Result
);

  wire adder_1_cout, or_1_out, subtractor_1_bout;
  wire [31:0] adder_1_out, subtractor_1_out;

  Adder #(.width(32)) adder_1 (.a(A), .b(B), .out(adder_1_out), .cin(1'b0), .cout(adder_1_cout));
  Subtractor #(.width(32)) subtractor_1 (.a(A), .b(B), .out(subtractor_1_out), .bin(1'b0), .bout(subtractor_1_bout));
  Multiplexer #(.select(2), .width(32)) multiplexer_1 (
    .in0(adder_1_out), .in2(subtractor_1_out), .out({Negative, Result[30:0]}), .sel(aluop));  // open: in1, in3
  Multiplexer #(.select(2)) multiplexer_2 (
    .in0(adder_1_cout), .in1(1'b0), .in2(subtractor_1_bout), .in3(1'b0), .out(Carry), .sel(aluop));
  or or_1 (or_1_out, Result[0], Result[1], Result[2], Result[3], Result[4], Result[5], Result[6], Result[7], Result[8], Result[9], Result[10], Result[11], Result[12], Result[13], Result[14], Result[15], Result[17], Result[18], Result[19], Result[20], Result[21], Result[22], Result[23], Result[24], Result[25], Result[26], Result[27], Result[28], Result[29], Result[30], Negative, Result[16]);
  not not_1 (Zero, or_1_out);

  assign Result[31] = Negative;

  // Notes on the sheet:
  //   32-bit ALU
endmodule
