// Logisim project Minimimo_v06_HardWired_EVO.circ as structural Verilog: 13 circuits, main circuit MiMo_v06
// address
module MiMo_v06 (
  input  ManualControl,
  input  Cycle,
  input  Instr,
  input  dwrite,
  input  [1:0] regsrc,
  input  [1:0] aluop,
  input  datawrite,
  input  irload,
  input  [1:0] addrsel,
  input  pcload,
  input  pcsel,
  input  Phase,
  input  Stop,
  input  [15:0] Addr
);

  wire and_1_out, and_2_out, and_3_out, and_4_out, c, Clear_out, ClearScr_out, CLK, CLKIN, Cont_out,
       datawrite_t, dwrite_t, FB_LED, irload_t, n, not_1_out, pcload_t, pcsel_t, Phase_t, RAMSel, reset,
       TTYSel, z;
  wire [1:0] addrsel_t, aluop_t, dregs, regsrc_t, sregs;
  wire [3:0] icycles, opcode, showhexa_1_digit, showhexa_1_out_2, showhexa_1_out_3, showhexa_1_out_5,
       showhexa_2_digit, showhexa_2_out_2, showhexa_2_out_3, showhexa_2_out_5;
  wire [15:0] address, aluout, cmds, cycles, data, decoder_1_out0, dreg, frame_buffer_16x16_1_out_6,
       frame_buffer_16x16_1_out_7, frame_buffer_16x16_1_out_8, frame_buffer_16x16_1_out_9,
       frame_buffer_16x16_1_out_10, frame_buffer_16x16_1_out_11, frame_buffer_16x16_1_out_12,
       frame_buffer_16x16_1_out_13, frame_buffer_16x16_1_out_14, frame_buffer_16x16_1_out_15,
       frame_buffer_16x16_1_out_16, frame_buffer_16x16_1_out_17, frame_buffer_16x16_1_out_18,
       frame_buffer_16x16_1_out_19, frame_buffer_16x16_1_out_20, frame_buffer_16x16_1_out_21, immed, irreg,
       multiplexer_1_out, pcreg, registerfile_1_r0, registerfile_1_r1, registerfile_1_r2, registerfile_1_r3,
       sreg;

  Button Cont (.out(Cont_out));
  PC pc_1 (.imreg(immed), .pcsel(pcsel_t), .pcload(pcload_t), .clock(CLK), .reset(reset), .pcout(pcreg));
  // Probe on multiplexer_1_out
  Multiplexer #(.select(2), .width(16)) multiplexer_1 (
    .in0(sreg), .in1(immed), .in2(data), .in3(aluout), .out(multiplexer_1_out), .sel(regsrc_t));
  // Probe on regsrc_t
  InstructionReg instructionreg_1 (
    .reset(reset), .irload(irload_t), .instruction(data), .clock(CLK), .sregsel(sregs), .dregsel(dregs),
    .opcode(opcode), .Instruction_register_Content(irreg), .immed(immed));
  // Probe on irreg
  Multiplexer #(.enable("true"), .select(2), .width(16)) multiplexer_2 (
    .in0(pcreg), .in1(immed), .in2(sreg), .in3(dreg), .out(address), .sel(addrsel_t));  // open: en
  // Probe on addrsel_t
  Registerfile registerfile_1 (
    .regval(multiplexer_1_out), .clock(CLK), .Reset(reset), .dsel(dregs), .ssel(sregs), .dwrite(dwrite_t),
    .dreg(dreg), .sreg(sreg), .r0(registerfile_1_r0), .r1(registerfile_1_r1), .r2(registerfile_1_r2),
    .r3(registerfile_1_r3), .Zero(z), .Negative(n));
  // Probe on sregs
  // Probe on dregs
  // Probe on immed
  // Probe on opcode
  Button u_Reset (.out(reset));
  Address_Decoder ADDR_DEC (.Address(address), .RAM(RAMSel), .FB_LED(FB_LED), .TTY(TTYSel));  // open: output_3
  // Probe on registerfile_1_r0
  // Probe on registerfile_1_r1
  // Probe on registerfile_1_r2
  // Probe on registerfile_1_r3
  ALU alu_1 (.A(dreg), .B(sreg), .aluop(aluop_t), .Result(aluout), .Carry(c));
  // Probe on dreg
  // Probe on sreg
  // Probe on aluop_t
  DebugUnit debugunit_1 (
    .reset(reset), .\continue (Cont_out), .clock(CLKIN), .pcreg(pcreg), .break_addr(Addr),
    .break_on_addr(Stop), .ucounter(Phase_t), .break_on_instr(Instr), .break_on_cycle(Cycle), .clock_out(CLK));
  Clock SysClk (.out(CLKIN));
  // Probe on aluout
  assign data = datawrite_t ? dreg : 16'bz;  // Controlled_Buffer controlled_buffer_1
  // Probe on Phase_t
  LED led_1 (.in(Phase_t));
  // Probe on regsrc_t
  LED led_2 (.in(dwrite_t));
  // Probe on pcreg
  Hex_Digit_Display hex_digit_display_1 (.value(showhexa_1_out_2));  // open: dp
  ShowHexa showhexa_1 (
    .Data(address), .Digit(showhexa_1_digit), .out_5(showhexa_1_out_5), .out_2(showhexa_1_out_2),
    .out_3(showhexa_1_out_3));
  Hex_Digit_Display hex_digit_display_2 (.value(showhexa_2_out_2));  // open: dp
  ShowHexa showhexa_2 (
    .Data(data), .Digit(showhexa_2_digit), .out_5(showhexa_2_out_5), .out_2(showhexa_2_out_2),
    .out_3(showhexa_2_out_3));
  LED led_3 (.in(Phase_t));
  // Probe on aluop_t
  LED led_4 (.in(datawrite_t));
  CtrlSigSwitch ctrlsigswitch_1 (
    .Select12(ManualControl), .dwrite1(dwrite), .regsrc1(regsrc), .aluop1(aluop), .datawrite1(datawrite),
    .irload1(irload), .addrsel1(addrsel), .pcload1(pcload), .pcsel1(pcsel), .Phase1(Phase), .opcode(opcode),
    .clock(CLK), .reset(reset), .Zero(z), .Negative(n), .dwrite(dwrite_t), .regsrc(regsrc_t),
    .aluop(aluop_t), .datawrite(datawrite_t), .irload(irload_t), .addrsel(addrsel_t), .pcload(pcload_t),
    .pcsel(pcsel_t), .Phase(Phase_t));
  // Probe on address
  Hex_Digit_Display hex_digit_display_3 (.value(showhexa_1_out_3));  // open: dp
  Hex_Digit_Display hex_digit_display_4 (.value(showhexa_1_digit));  // open: dp
  LED led_5 (.in(datawrite_t));
  LED led_6 (.in(datawrite_t));
  Hex_Digit_Display hex_digit_display_5 (.value(showhexa_2_out_3));  // open: dp
  Hex_Digit_Display hex_digit_display_6 (.value(showhexa_2_digit));  // open: dp
  // Probe on datawrite_t
  LED led_7 (.in(datawrite_t));
  LED led_8 (.in(datawrite_t));
  LED led_9 (.in(irload_t));
  // Probe on data
  Hex_Digit_Display hex_digit_display_7 (.value(showhexa_1_out_5));  // open: dp
  // Probe on RAMSel
  // Probe on datawrite_t
  // Probe on TTYSel
  // Probe on FB_LED
  Hex_Digit_Display hex_digit_display_8 (.value(showhexa_2_out_5));  // open: dp
  // Probe on addrsel_t
  LED led_10 (.in(pcload_t));
  // Probe on opcode
  // Probe on dregs
  LED u_C (.in(c));
  LED u_Z (.in(z));
  LED u_N (.in(n));
  LED led_11 (.in(pcsel_t));
  LED led_12 (.in(Phase_t));
  // Probe on irreg
  // Probe on sregs
  // Probe on immed
  not not_1 (not_1_out, datawrite_t);
  RAM #(.addrWidth(14), .asyncread("true"), .dataWidth(16), .databus("bidir"), .\type ("nonvolatile")) ram_1 (
    .addr(address[13:0]), .we(and_1_out), .oe(and_2_out), .clk(CLK), .data(data));
  and and_1 (and_1_out, RAMSel, datawrite_t);
  and and_2 (and_2_out, RAMSel, not_1_out);
  // Probe on pcreg
  Decoder #(.enable("false"), .select(4)) decoder_1 (
    .out0(decoder_1_out0[0]), .out1(decoder_1_out0[1]), .out2(decoder_1_out0[2]), .out3(decoder_1_out0[3]),
    .out4(decoder_1_out0[4]), .out5(decoder_1_out0[5]), .out6(decoder_1_out0[6]), .out7(decoder_1_out0[7]),
    .out8(decoder_1_out0[8]), .out9(decoder_1_out0[9]), .out10(decoder_1_out0[10]),
    .out11(decoder_1_out0[11]), .out12(decoder_1_out0[12]), .out13(decoder_1_out0[13]),
    .out14(decoder_1_out0[14]), .out15(decoder_1_out0[15]), .sel(opcode));
  // Probe on data[6:0]
  DotMatrix #(.inputtype("row"), .matrixcols(16), .matrixrows(16)) dotmatrix_1 (
    .row0(frame_buffer_16x16_1_out_21), .row1(frame_buffer_16x16_1_out_20),
    .row2(frame_buffer_16x16_1_out_19), .row3(frame_buffer_16x16_1_out_18),
    .row4(frame_buffer_16x16_1_out_17), .row5(frame_buffer_16x16_1_out_16),
    .row6(frame_buffer_16x16_1_out_15), .row7(frame_buffer_16x16_1_out_14),
    .row8(frame_buffer_16x16_1_out_13), .row9(frame_buffer_16x16_1_out_12),
    .row10(frame_buffer_16x16_1_out_11), .row11(frame_buffer_16x16_1_out_10),
    .row12(frame_buffer_16x16_1_out_9), .row13(frame_buffer_16x16_1_out_8),
    .row14(frame_buffer_16x16_1_out_7), .row15(frame_buffer_16x16_1_out_6));
  Frame_Buffer_16x16 frame_buffer_16x16_1 (
    .address(address[3:0]), .store(and_3_out), .data(data), .clock(CLK), .reset(Clear_out),
    .out_6(frame_buffer_16x16_1_out_6), .out_7(frame_buffer_16x16_1_out_7),
    .out_8(frame_buffer_16x16_1_out_8), .out_9(frame_buffer_16x16_1_out_9),
    .out_10(frame_buffer_16x16_1_out_10), .out_11(frame_buffer_16x16_1_out_11),
    .out_12(frame_buffer_16x16_1_out_12), .out_13(frame_buffer_16x16_1_out_13),
    .out_14(frame_buffer_16x16_1_out_14), .out_15(frame_buffer_16x16_1_out_15),
    .out_16(frame_buffer_16x16_1_out_16), .out_17(frame_buffer_16x16_1_out_17),
    .out_18(frame_buffer_16x16_1_out_18), .out_19(frame_buffer_16x16_1_out_19),
    .out_20(frame_buffer_16x16_1_out_20), .out_21(frame_buffer_16x16_1_out_21));
  and and_3 (and_3_out, FB_LED, datawrite_t);
  LED led_13 (.in(decoder_1_out0[0]));
  LED led_14 (.in(decoder_1_out0[1]));
  LED led_15 (.in(decoder_1_out0[2]));
  LED led_16 (.in(decoder_1_out0[3]));
  LED led_17 (.in(decoder_1_out0[4]));
  LED led_18 (.in(decoder_1_out0[5]));
  LED led_19 (.in(decoder_1_out0[6]));
  LED led_20 (.in(decoder_1_out0[7]));
  LED led_21 (.in(decoder_1_out0[8]));
  LED led_22 (.in(decoder_1_out0[9]));
  LED led_23 (.in(decoder_1_out0[10]));
  LED led_24 (.in(decoder_1_out0[11]));
  LED led_25 (.in(decoder_1_out0[12]));
  LED led_26 (.in(decoder_1_out0[13]));
  LED led_27 (.in(decoder_1_out0[14]));
  LED led_28 (.in(decoder_1_out0[15]));
  // Probe on cmds
  TTY #(.cols(16), .rows(4)) tty_1 (.data(data[6:0]), .clk(CLK), .we(and_4_out), .clr(ClearScr_out));
  Button ClearScr (.out(ClearScr_out));
  and and_4 (and_4_out, TTYSel, datawrite_t);
  Button Clear (.out(Clear_out));
  // Probe on cycles
  Counters counters_1 (
    .new_ucounter(Phase_t), .reset(reset), .clock(CLK), .cmds(cmds), .cycles(cycles), .icycles(icycles));
  // Probe on dregs
  // Probe on immed
  // Probe on sregs

  // Other names for the same wires on the sheet: dbgadr = Stop

  // Notes on the sheet:
  //   Quick tips:
  //   IR
  //   Registers
  //   Debug
  //   Breakpoint
  //   Use ctrl+t to manually toggle global clock signal
  //   Use Simulate->Ticks Enabled for automatic clock signal
  //   Mini MiMo - Hardwired Simple CPU Model
  //   1 Write Rd
  //   Based on: https://minnie.tuhs.org/CompArch/Tutes/week03.html
  //   v05: Migration to EVO, Debug, Counters, ImmReg Units
  //   Fetch
  //   0 Rs
  //   1 IMM
  //   2 DBus
  //   3 ALU
  //   Execute
  //   0 AND
  //   1 Write
  //   1 ORR
  //   2 ADD
  //   3 SUB
  //   v0.6 EVO
  //   Address
  //   Address BUS
  //   Control BUS
  //   Read
  //   Write
  //   Data BUS
  //   Read
  //   Write
  //   Control signals
  //   Control Unit
  //   1 Write
  //   v06: More V.N. model like design (CPU,Mem,IO,..)
  //   Data
  //   0 PC
  //   1 Write
  //   1 IMM
  //   2 Rs
  //   3 Rd
  //   Instruction:
  //   Rd
  //   Flags
  //   0 IMM
  //   1 pc+1
  //   Rs
  //   immed 
  //   0 Fetch
  //   1 Execute
  //   PC
  //   RAM
  //   TTY
  //   NOP 
  //   Frame Buffer LED 16x16
  //   AND Rd, Rd, Rs 
  //   ORR  Rd, Rd, Rs
  //   ADD Rd, Rd, Rs 
  //   SUB Rd, Rd, Rs
  //   LDRH  Rd, [Rs]
  //   STRH  Rd, [Rs] 
  //   MOV Rd, Rs 
  //   BEQ Rd, immed 
  //   BNE Rd, immed
  //   BGT Rd, immed 
  //   BLT Rd, immed 
  //   LDRH  Rd, [#immed] 
  //   STRH  Rd, [#immed] 
  //   MOV  Rd, #immed
  //   B immed
endmodule

module InstructionReg (
  input  [15:0] instruction,
  input  reset,
  input  clock,
  input  irload,
  output [15:0] immed,
  output [1:0] sregsel,
  output [1:0] dregsel,
  output [3:0] opcode,
  output [15:0] Instruction_register_Content
);

  Register #(.width(16)) register_1 (
    .D(instruction), .en(irload),
    .Q({Instruction_register_Content[15:12], dregsel, Instruction_register_Content[9:0]}), .clk(clock),
    .clr(reset));
  assign immed = {{8{1'b0}}, Instruction_register_Content[7:0]};  // Bit_Extender bit_extender_1

  assign Instruction_register_Content[11:10] = dregsel;
  assign opcode = Instruction_register_Content[15:12];
  assign sregsel = Instruction_register_Content[9:8];

  // Notes on the sheet:
  //   IR Logic
endmodule

module Registerfile (
  input  [15:0] regval,
  input  Reset,
  input  [1:0] dsel,
  input  [1:0] ssel,
  input  dwrite,
  input  clock,
  output [15:0] r0,
  output [15:0] r1,
  output [15:0] r2,
  output [15:0] r3,
  output Zero,
  output [15:0] dreg,
  output [15:0] sreg,
  output Negative
);

  wire demultiplexer_1_out0, demultiplexer_1_out1, demultiplexer_1_out2, demultiplexer_1_out3, or_1_out;

  Demultiplexer #(.select(2)) demultiplexer_1 (
    .out0(demultiplexer_1_out0), .out1(demultiplexer_1_out1), .out2(demultiplexer_1_out2),
    .out3(demultiplexer_1_out3), .in(dwrite), .sel(dsel));
  // Probe on regval
  // Probe on regval
  // Probe on dsel
  // Probe on ssel
  Register #(.width(16)) register_1 (.D(regval), .en(demultiplexer_1_out0), .Q(r0), .clk(clock), .clr(Reset));
  Register #(.width(16)) register_2 (.D(regval), .en(demultiplexer_1_out1), .Q(r1), .clk(clock), .clr(Reset));
  Register #(.width(16)) register_3 (.D(regval), .en(demultiplexer_1_out2), .Q(r2), .clk(clock), .clr(Reset));
  Register #(.width(16)) register_4 (.D(regval), .en(demultiplexer_1_out3), .Q(r3), .clk(clock), .clr(Reset));
  Multiplexer #(.select(2), .width(16)) multiplexer_1 (.in0(r0), .in1(r1), .in2(r2), .in3(r3), .out(dreg), .sel(dsel));
  // Probe on dreg
  Multiplexer #(.select(2), .width(16)) multiplexer_2 (.in0(r0), .in1(r1), .in2(r2), .in3(r3), .out(sreg), .sel(ssel));
  // Probe on sreg
  // Probe on r0
  // Probe on r0
  // Probe on r1
  // Probe on r1
  // Probe on r2
  // Probe on r2
  // Probe on r3
  // Probe on r3
  or or_1 (or_1_out, dreg[0], dreg[1], dreg[2], dreg[3], dreg[4], dreg[5], dreg[6], dreg[7], dreg[9], dreg[10], dreg[11], dreg[12], dreg[13], dreg[14], dreg[15], dreg[8]);
  not not_1 (Zero, or_1_out);

  assign Negative = dreg[15];

  // Notes on the sheet:
  //   Rd select
  //   Rs select
  //   Register File
  //   Rd
  //   R0
  //   R1
  //   R2
  //   R3
  //   Rs
endmodule

module ALU (
  input  [15:0] A,
  input  [15:0] B,
  input  [1:0] aluop,
  output Carry,
  output [15:0] Result
);

  wire adder_1_cout, subtractor_1_bout;
  wire [15:0] adder_1_out, and_1_out, or_1_out, subtractor_1_out;

  // Probe on A
  // Probe on B
  Subtractor #(.width(16)) subtractor_1 (.a(A), .b(B), .out(subtractor_1_out), .bin(1'b0), .bout(subtractor_1_bout));
  Adder #(.width(16)) adder_1 (.a(A), .b(B), .out(adder_1_out), .cin(1'b0), .cout(adder_1_cout));
  assign or_1_out = A | B;  // OR_Gate or_1, 16 bits wide
  assign and_1_out = A & B;  // AND_Gate and_1, 16 bits wide
  // Probe on subtractor_1_out
  // Probe on subtractor_1_out
  // Probe on adder_1_out
  // Probe on adder_1_out
  // Probe on or_1_out
  // Probe on or_1_out
  // Probe on and_1_out
  // Probe on and_1_out
  Multiplexer #(.select(2), .width(16)) multiplexer_1 (
    .in0(and_1_out), .in1(or_1_out), .in2(adder_1_out), .in3(subtractor_1_out), .out(Result), .sel(aluop));
  Multiplexer #(.select(2)) multiplexer_2 (
    .in0(1'b0), .in1(1'b0), .in2(adder_1_cout), .in3(subtractor_1_bout), .out(Carry), .sel(aluop));
  // Probe on Result
  // Probe on Result

  // Notes on the sheet:
  //   16-bit ALU
  //   Signed
  //   Unsigned
endmodule

module PC (
  input  [15:0] imreg,
  input  pcload,
  input  clock,
  input  reset,
  input  pcsel,
  output [15:0] pcout
);

  wire [15:0] adder_1_out, multiplexer_1_out;

  Adder #(.width(16)) adder_1 (.a(pcout), .b(16'h1), .out(adder_1_out));  // open: cin, cout
  Multiplexer #(.width(16)) multiplexer_1 (.in0(imreg), .in1(adder_1_out), .out(multiplexer_1_out), .sel(pcsel));
  Register #(.width(16)) register_1 (.D(multiplexer_1_out), .en(pcload), .Q(pcout), .clk(clock), .clr(reset));

  // Notes on the sheet:
  //   PC Logic
endmodule

module ShowHexa (
  input  [15:0] Data,
  output [3:0] out_2,
  output [3:0] out_3,
  output [3:0] Digit,
  output [3:0] out_5
);


  assign Digit = Data[7:4];
  assign out_2 = Data[15:12];
  assign out_3 = Data[11:8];
  assign out_5 = Data[3:0];
endmodule

module Frame_Buffer_16x16 (
  input  [3:0] address,
  input  store,
  input  [15:0] data,
  input  clock,
  input  reset,
  output [15:0] out_6,
  output [15:0] out_7,
  output [15:0] out_8,
  output [15:0] out_9,
  output [15:0] out_10,
  output [15:0] out_11,
  output [15:0] out_12,
  output [15:0] out_13,
  output [15:0] out_14,
  output [15:0] out_15,
  output [15:0] out_16,
  output [15:0] out_17,
  output [15:0] out_18,
  output [15:0] out_19,
  output [15:0] out_20,
  output [15:0] out_21
);

  wire demultiplexer_1_out0, demultiplexer_1_out1, demultiplexer_1_out2, demultiplexer_1_out3,
       demultiplexer_1_out4, demultiplexer_1_out5, demultiplexer_1_out6, demultiplexer_1_out7,
       demultiplexer_1_out8, demultiplexer_1_out9, demultiplexer_1_out10, demultiplexer_1_out11,
       demultiplexer_1_out12, demultiplexer_1_out13, demultiplexer_1_out14, demultiplexer_1_out15;

  Demultiplexer #(.select(4)) demultiplexer_1 (
    .out0(demultiplexer_1_out0), .out1(demultiplexer_1_out1), .out2(demultiplexer_1_out2),
    .out3(demultiplexer_1_out3), .out4(demultiplexer_1_out4), .out5(demultiplexer_1_out5),
    .out6(demultiplexer_1_out6), .out7(demultiplexer_1_out7), .out8(demultiplexer_1_out8),
    .out9(demultiplexer_1_out9), .out10(demultiplexer_1_out10), .out11(demultiplexer_1_out11),
    .out12(demultiplexer_1_out12), .out13(demultiplexer_1_out13), .out14(demultiplexer_1_out14),
    .out15(demultiplexer_1_out15), .in(store), .sel(address));
  Register #(.width(16)) register_1 (.D(data), .en(demultiplexer_1_out0), .Q(out_6), .clk(clock), .clr(reset));
  Register #(.width(16)) register_2 (.D(data), .en(demultiplexer_1_out1), .Q(out_7), .clk(clock), .clr(reset));
  Register #(.width(16)) register_3 (.D(data), .en(demultiplexer_1_out2), .Q(out_8), .clk(clock), .clr(reset));
  Register #(.width(16)) register_4 (.D(data), .en(demultiplexer_1_out3), .Q(out_9), .clk(clock), .clr(reset));
  Register #(.width(16)) register_5 (.D(data), .en(demultiplexer_1_out4), .Q(out_10), .clk(clock), .clr(reset));
  Register #(.width(16)) register_6 (.D(data), .en(demultiplexer_1_out5), .Q(out_11), .clk(clock), .clr(reset));
  Register #(.width(16)) register_7 (.D(data), .en(demultiplexer_1_out6), .Q(out_12), .clk(clock), .clr(reset));
  Register #(.width(16)) register_8 (.D(data), .en(demultiplexer_1_out7), .Q(out_13), .clk(clock), .clr(reset));
  Register #(.width(16)) register_9 (.D(data), .en(demultiplexer_1_out8), .Q(out_14), .clk(clock), .clr(reset));
  Register #(.width(16)) register_10 (.D(data), .en(demultiplexer_1_out9), .Q(out_15), .clk(clock), .clr(reset));
  Register #(.width(16)) register_11 (.D(data), .en(demultiplexer_1_out10), .Q(out_16), .clk(clock), .clr(reset));
  Register #(.width(16)) register_12 (.D(data), .en(demultiplexer_1_out11), .Q(out_17), .clk(clock), .clr(reset));
  Register #(.width(16)) register_13 (.D(data), .en(demultiplexer_1_out12), .Q(out_18), .clk(clock), .clr(reset));
  Register #(.width(16)) register_14 (.D(data), .en(demultiplexer_1_out13), .Q(out_19), .clk(clock), .clr(reset));
  Register #(.width(16)) register_15 (.D(data), .en(demultiplexer_1_out14), .Q(out_20), .clk(clock), .clr(reset));
  Register #(.width(16)) register_16 (.D(data), .en(demultiplexer_1_out15), .Q(out_21), .clk(clock), .clr(reset));
endmodule

module Address_Decoder (
  input  [15:0] Address,
  output RAM,
  output FB_LED,
  output TTY,
  output output_3
);

  Decoder #(.select(2)) decoder_1 (
    .out0(RAM), .out1(FB_LED), .out2(TTY), .out3(output_3), .sel(Address[15:14]), .en(1'b1));
endmodule

module Counters (
  input  new_ucounter,
  input  reset,
  input  clock,
  output [15:0] cycles,
  output [3:0] icycles,
  output [15:0] cmds
);

  wire not_1_out;

  not not_1 (not_1_out, new_ucounter);
  Counter #(.max('hffff), .width(16)) counter_1 (
    .Q(cycles), .clk(clock), .clr(reset));  // open: load, D, count, carry, up
  Counter #(.max('hf), .width(4)) counter_2 (
    .load(not_1_out), .D(4'b0000), .Q(icycles), .clk(clock), .clr(reset));  // open: count, carry, up
  Counter #(.max('hffff), .width(16)) counter_3 (
    .count(not_1_out), .Q(cmds), .clk(clock), .clr(reset));  // open: load, D, carry, up
  // Probe on cycles
  // Probe on icycles
  // Probe on cmds

  // Notes on the sheet:
  //   Counts the number of clock cycles
  //   since the start.
  //   Counts the number of clock cycles
  //   since the start of current instruction.
  //   Counts the number of instructions
  //   since the start.
  //   Cycle/Cmds Counters
endmodule

module DebugUnit (
  input  reset,
  input  \continue ,
  input  clock,
  input  [15:0] pcreg,
  input  [15:0] break_addr,
  input  break_on_addr,
  input  ucounter,
  input  break_on_instr,
  input  break_on_cycle,
  output clock_out
);

  wire and_1_out, and_2_out, and_3_out, nor_1_out, nor_2_out, not_1_out, or_1_out, shift_register_1_out,
       shift_register_1_q0;
  wire [15:0] xor_1_out;

  Shift_Register #(.length(2), .trigger("falling")) shift_register_1 (
    .in(\continue ), .clk(clock), .out(shift_register_1_out), .clr(reset), .q0(shift_register_1_q0));  // open: shift, load, d0, d1, q1
  assign xor_1_out = pcreg ^ break_addr;  // XOR_Gate xor_1, 16 bits wide
  LED Addr (.in(break_on_addr));
  not not_1 (not_1_out, ucounter);
  and and_1 (and_1_out, ~shift_register_1_out, shift_register_1_q0);  // AND_Gate
  nor nor_1 (nor_1_out, xor_1_out[15], xor_1_out[14], xor_1_out[13], xor_1_out[12], xor_1_out[11], xor_1_out[10], xor_1_out[9], xor_1_out[8], xor_1_out[6], xor_1_out[5], xor_1_out[4], xor_1_out[3], xor_1_out[2], xor_1_out[1], xor_1_out[0], xor_1_out[7]);
  and and_2 (and_2_out, nor_1_out, break_on_addr, not_1_out);
  and and_3 (and_3_out, not_1_out, break_on_instr);
  LED Instr (.in(break_on_instr));
  LED Cycle (.in(break_on_cycle));
  nor nor_2 (nor_2_out, and_2_out, and_3_out, break_on_cycle);
  or or_1 (or_1_out, and_1_out, nor_2_out);
  LED Pass (.in(or_1_out));
  and and_4 (clock_out, clock, or_1_out);

  // Notes on the sheet:
  //   Breaks on PC = break_addr
  //   Breaks on each new instruction
  //   Breaks on each clock pulse
  //   Makes sure the 'continue' button only
  //   lets through 1 clock pulse, until you let go
  //   and press it again.
  //   Outputs 1 only on first cycle (shift bits are unequal).
  //   Debug Unit
  //   PC = break_addr?
endmodule

module ControlUnit_HW (
  input  [3:0] opcode,
  input  clock,
  input  reset,
  input  zero,
  input  negative,
  output phase,
  output [1:0] aluop,
  output pcsel,
  output irload,
  output readwrite,
  output pcload,
  output [1:0] regsel,
  output dwrite,
  output [1:0] addrsel
);

  wire and_1_out, and_2_out, and_3_out, and_4_out, multiplexer_3_out, multiplexer_6_out, not_1_out,
       not_2_out, not_3_out, not_4_out, or_1_out;
  wire [1:0] multiplexer_1_out, multiplexer_10_out;

  not not_1 (not_1_out, zero);
  not not_2 (not_2_out, negative);
  and and_1 (and_1_out, not_1_out, not_2_out);
  Multiplexer #(.enable("true"), .select(4), .width(2)) multiplexer_1 (
    .in0(2'b11), .in1(2'b11), .in2(2'b11), .in3(2'b11), .in4(2'b10), .in5(2'b00), .in6(2'b01), .in7(2'b00),
    .in8(2'b00), .in9(2'b00), .in10(2'b00), .in11(2'b00), .in12(2'b10), .in13(2'b00), .in14(2'b01),
    .in15(2'b00), .out(multiplexer_1_out), .sel(opcode));  // open: en
  Multiplexer multiplexer_2 (.in0(1'b1), .in1(1'b0), .out(irload), .sel(phase));
  not not_3 (not_3_out, opcode[2]);
  Multiplexer #(.enable("true"), .select(2)) multiplexer_3 (
    .in0(zero), .in1(not_1_out), .in2(and_1_out), .in3(negative), .out(multiplexer_3_out), .sel(opcode[1:0]));  // open: en
  and and_2 (and_2_out, not_3_out, opcode[3], multiplexer_3_out);
  and and_3 (and_3_out, opcode[0], opcode[1], opcode[2], opcode[3]);
  Multiplexer #(.enable("true"), .width(2)) multiplexer_4 (
    .in0(2'b00), .in1(multiplexer_1_out), .out(regsel), .sel(phase));  // open: en
  or or_1 (or_1_out, and_2_out, and_3_out);
  Multiplexer #(.enable("true")) multiplexer_5 (.in0(1'b1), .in1(or_1_out), .out(pcload), .sel(phase));  // open: en
  Multiplexer #(.enable("true"), .select(4)) multiplexer_6 (
    .in0(1'b1), .in1(1'b1), .in2(1'b1), .in3(1'b1), .in4(1'b1), .in5(1'b0), .in6(1'b1), .in7(1'b0),
    .in8(1'b0), .in9(1'b0), .in10(1'b0), .in11(1'b0), .in12(1'b1), .in13(1'b0), .in14(1'b1), .in15(1'b0),
    .out(multiplexer_6_out), .sel(opcode));  // open: en
  not not_4 (not_4_out, opcode[1]);
  Multiplexer #(.enable("true")) multiplexer_7 (
    .in0(1'b0), .in1(multiplexer_6_out), .out(dwrite), .sel(phase));  // open: en
  Counter #(.max('h1), .width(1)) counter_1 (
    .Q(phase), .up(1'b1), .clk(clock), .clr(reset));  // open: load, D, count, carry
  Multiplexer #(.enable("true")) multiplexer_8 (.in0(1'b1), .in1(1'b0), .out(pcsel), .sel(phase));  // open: en
  and and_4 (and_4_out, opcode[0], not_4_out, opcode[2]);
  Multiplexer #(.enable("true")) multiplexer_9 (.in0(1'b0), .in1(and_4_out), .out(readwrite), .sel(phase));  // open: en
  Multiplexer #(.enable("true"), .select(4), .width(2)) multiplexer_10 (
    .in0(2'b00), .in1(2'b00), .in2(2'b00), .in3(2'b00), .in4(2'b10), .in5(2'b10), .in6(2'b00), .in7(2'b00),
    .in8(2'b00), .in9(2'b00), .in10(2'b00), .in11(2'b00), .in12(2'b00), .in13(2'b01), .in14(2'b01),
    .in15(2'b00), .out(multiplexer_10_out), .sel(opcode));  // open: en
  Multiplexer #(.enable("true"), .width(2)) multiplexer_11 (
    .in0(2'b00), .in1(multiplexer_10_out), .out(addrsel), .sel(phase));  // open: en

  assign aluop = opcode[1:0];

  // Other names for the same wires on the sheet: irbit4 = opcode[0]; op1op2[3:0] = opcode; op2[1:0] = opcode[1:0];
  //   irbit5 = opcode[1]; irbit6 = opcode[2]; op1[1:0] = opcode[3:2]; irbit7 = opcode[3]

  // Notes on the sheet:
  //   IR Load
  //   PC Load
  //   Register Select
  //   Dest Reg Write
  //   Phase counter
  //   PC Select
  //   Read/Write
  //   Address Select
endmodule

module CtrlSigSwitch (
  input  Select12,
  input  dwrite1,
  input  [1:0] regsrc1,
  input  [1:0] aluop1,
  input  datawrite1,
  input  irload1,
  input  [1:0] addrsel1,
  input  pcload1,
  input  pcsel1,
  input  Phase1,
  input  [3:0] opcode,
  input  clock,
  input  reset,
  input  Zero,
  input  Negative,
  output dwrite,
  output [1:0] regsrc,
  output [1:0] aluop,
  output datawrite,
  output irload,
  output [1:0] addrsel,
  output pcload,
  output pcsel,
  output Phase
);

  wire [1:0] controlunit_hw_1_addrsel, controlunit_hw_1_aluop, controlunit_hw_1_regsel;
  wire [11:0] controlunit_hw_1_dwrite;

  ControlUnit_HW controlunit_hw_1 (
    .opcode(opcode), .clock(clock), .reset(reset), .zero(Zero), .negative(Negative),
    .phase(controlunit_hw_1_dwrite[11]), .aluop(controlunit_hw_1_aluop), .pcsel(controlunit_hw_1_dwrite[10]),
    .irload(controlunit_hw_1_dwrite[6]), .readwrite(controlunit_hw_1_dwrite[5]),
    .pcload(controlunit_hw_1_dwrite[9]), .regsel(controlunit_hw_1_regsel),
    .dwrite(controlunit_hw_1_dwrite[0]), .addrsel(controlunit_hw_1_addrsel));
  Multiplexer #(.width(12)) multiplexer_1 (
    .in0({controlunit_hw_1_dwrite[11:9], controlunit_hw_1_addrsel, controlunit_hw_1_dwrite[6:5], controlunit_hw_1_aluop, controlunit_hw_1_regsel, controlunit_hw_1_dwrite[0]}),
    .in1({Phase1, pcsel1, pcload1, addrsel1, irload1, datawrite1, aluop1, regsrc1, dwrite1}),
    .out({Phase, pcsel, pcload, addrsel, irload, datawrite, aluop, regsrc, dwrite}), .sel(Select12));
endmodule

module CtrlSigSwitch2 (
  input  Select12,
  input  dwrite1,
  input  [1:0] regsrc1,
  input  [1:0] aluop1,
  input  datawrite1,
  input  irload1,
  input  [1:0] addrsel1,
  input  pcload1,
  input  pcsel1,
  input  Phase1,
  input  dwrite2,
  input  [1:0] regsrc2,
  input  [1:0] aluop2,
  input  datawrite2,
  input  irload2,
  input  [1:0] addrsel2,
  input  pcload2,
  input  pcsel2,
  input  Phase2,
  output dwrite,
  output [1:0] regsrc,
  output [1:0] aluop,
  output datawrite,
  output irload,
  output [1:0] addrsel,
  output pcload,
  output pcsel,
  output Phase
);

  Multiplexer #(.width(12)) multiplexer_1 (
    .in0({Phase1, pcsel1, pcload1, addrsel1, irload1, datawrite1, aluop1, regsrc1, dwrite1}),
    .in1({Phase2, pcsel2, pcload2, addrsel2, irload2, datawrite2, aluop2, regsrc2, dwrite2}),
    .out({Phase, pcsel, pcload, addrsel, irload, datawrite, aluop, regsrc, dwrite}), .sel(Select12));
endmodule
